# Fritzing sketch DistanceGuesser (saved by Fritzing 0.9.10b)
breadboards: 1

parts:
  Part1 = Arduino Nano 33 IOT  # not connected
  HC-SR04_Sensor_1 = HC-SR04 Ultrasonic Distance Sensor
  R1 = Resistor [tolerance=±5% resistance=1k package="0805 [SMD]"]
  R2 = Resistor [tolerance=±5% resistance=1k package="0805 [SMD]"]
  R3 = Resistor [tolerance=±5% resistance=220 package="0805 [SMD]"]
  R4 = Resistor [tolerance=±5% resistance=220 package="0805 [SMD]"]
  S1 = Pushbutton [package="[SMD]"]
  R5 = Resistor [tolerance=±5% resistance=10k package="0805 [SMD]"]
  LED1 = LED - 3mm [color="Red (633nm)" current=0.030 package="3 mm [THT]"]
  LED2 = LED - 3mm [color="Green (555nm)" current=0.030 package="3 mm [THT]"]

nets:
  N1: HC-SR04_Sensor_1.ECHO, R1.Pin_1
  N2: HC-SR04_Sensor_1.GND, R3.Pin_0, R5.Pin_0
  N3: R1.Pin_0, R2.Pin_1
  N4: R2.Pin_0, R4.Pin_1
  N5: R3.Pin_1, LED1.cathode
  N6: R4.Pin_0, LED2.cathode
  N7: S1.Pin_1, S1.Pin_2, R5.Pin_1
  N8: S1.Pin_3, S1.Pin_4

notes:
  Distance Guessing Game
  Ground connections
  Power connections
  GND
  3v3

custom parts:
  Arduino Nano 33 IOT: The Arduino Nano 33 IoT is the easiest and cheapest point of entry to enhance existing devices (and creating new ones) to be part of the IoT and designing pico-network applications. Whether you are looking at building a sensor network connected to your office or home router, or if you want to create a BLE device sending data to a cellphone, the Nano 33 IoT is your one-stop-solution for many of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
